# Fritzing sketch MyLifeIsPatate (saved by Fritzing 0.9.2b)
circuit board: 5.78986cm x 5.5711cm
breadboards: 1

parts:
  Arduino = Arduino BT
  R2 = Resistor [tolerance=±5% resistance=220 package="0805 [SMD]"]
  L1 = Inductor [package="400 mil [THT]"]
  C1 = Ceramic Capacitor [capacitance=10nF package="1206 [SMD, multilayer]"]
  D1 = Rectifier Diode [part_number=1N4001 package="Melf DO-213 AB [SMD]"]
  R1 = Resistor [tolerance=±5% resistance=10k package="0805 [SMD]"]
  C2 = Ceramic Capacitor [capacitance=10nF package="1206 [SMD, multilayer]"]
  POMME_DE_TERRE = TOUCH [package=touch2]

nets:
  N1: Arduino.PWM_D9, R1.Pin_0
  N2: Arduino.A0, R2.Pin_1, D1.cathode, C2.0
  N3: Arduino.GND, R2.Pin_0, C2.1
  N4: L1.pin_0, R1.Pin_1
  N5: L1.pin_1, C1.0, D1.anode
  N6: C1.1, POMME_DE_TERRE.T2
